// Digital circuit T1A0.dig as structural Verilog
module T1A0 (
  input  J0,
  input  J1,
  input  J2,
  input  J3,
  input  EN0,
  output S0
);

  wire or_1_out, or_2_out;

  or or_1 (or_1_out, J0, J1);
  or or_2 (or_2_out, or_1_out, J2);
  or or_3 (S0, or_2_out, J3);
endmodule
