// Digital circuit T1A2.dig as structural Verilog
module T1A2 (
  input  J0,
  input  J1,
  input  J2,
  input  J3,
  input  EN0,
  input  P,
  output S0
);

  wire and_1_out, not_1_out, not_2_out, or_1_out, or_2_out, or_3_out;

  not not_1 (not_1_out, J2);
  not not_2 (not_2_out, J3);
  or or_1 (or_1_out, J0, J1);
  or or_2 (or_2_out, not_1_out, not_2_out);
  or or_3 (or_3_out, or_1_out, or_2_out);
  and and_1 (and_1_out, or_3_out, EN0);
  or or_4 (S0, and_1_out, P);
endmodule
