// Digital circuit T3A1.dig as structural Verilog
module T3A1 (
  input  S0,
  input  S1,
  input  S2,
  output P
);

  wire and_1_out, and_2_out, and_3_out, not_1_out, not_2_out, or_1_out, or_2_out;

  not not_1 (not_1_out, S0);
  and and_1 (and_1_out, not_1_out, S1);
  and and_2 (and_2_out, S0, not_2_out);
  not not_2 (not_2_out, S1);
  or or_1 (or_1_out, and_1_out, and_2_out);
  or or_2 (or_2_out, or_1_out, S2);
  and and_3 (and_3_out, S0, S1);
  or or_3 (P, or_2_out, and_3_out);
endmodule
